# Fritzing sketch vfobfo_schematic (saved by Fritzing 0.9.3b)
breadboards: 1

parts:
  ARDUINO1 = Arduino Micro
  part = OLED Monochrome 128x64 0.96 inch [part_number=.]
  part_2 = Adafruit Si5351A Clock Generator [part_number=.]
  RE1 = Rotary Encoder [package=THT]
  R1 = Resistor [tolerance=±5% resistance=10k package="0805 [SMD]"]
  R2 = Resistor [tolerance=±5% resistance=10k package="0805 [SMD]"]
  R3 = Resistor [tolerance=±5% resistance=10k package="0805 [SMD]"]
  R5 = Resistor [tolerance=±5% resistance=10k package="0805 [SMD]"]
  R6 = Resistor [tolerance=±5% resistance=10k package="0805 [SMD]"]
  R7 = Resistor [tolerance=±5% resistance=10k package="0805 [SMD]"]
  C1 = Ceramic Capacitor [capacitance=10nF package="100 mil [THT, multilayer]"]
  C2 = Ceramic Capacitor [capacitance=10nF package="100 mil [THT, multilayer]"]
  S1 = SWITCH-MOMENTARY-2 [package=tactile-pth]
  S2 = SWITCH-MOMENTARY-2 [package=tactile-pth]
  S3 = SWITCH-MOMENTARY-2 [package=tactile-pth]
  part_3 = smd LED [color="Red (633nm)" package="0805 [SMD]"]
  R8 = Resistor [tolerance=±5% resistance=1k package="0805 [SMD]"]
  R4 = Resistor [tolerance=±5% resistance=10k package="0805 [SMD]"]

nets:
  N1: ARDUINO1.TX, R5.Pin_1, S2.1
  N2: ARDUINO1.RX, S1.1, R4.Pin_1
  N3: ARDUINO1.D2, part.MOSI_SDA, part_2.SDA
  N4: ARDUINO1.D3, part.SCLK_SCK, part_2.SCL
  N5: ARDUINO1.D7, R3.Pin_1, S3.1
  N6: ARDUINO1.D8, R2.Pin_0, C2.1
  N7: ARDUINO1.D9, R1.Pin_0, C1.0
  N8: ARDUINO1.D10, R8.Pin_0
  GND: ARDUINO1.GND, part.GND, part_2.GND, RE1.EncoderPinC, R3.Pin_0, R5.Pin_0, C1.1, C2.0, part_3.cathode, R4.Pin_0
  5V: ARDUINO1.VIN, part.VIN, part_2.VIN, R6.Pin_1, R7.Pin_1, S1.2, S2.2, S3.2
  N9: RE1.EncoderPinA, R2.Pin_1, R7.Pin_0
  N10: RE1.EncoderPinB, R1.Pin_1, R6.Pin_0
  N11: part_3.anode, R8.Pin_1

notes:
  Band
  Step
  Switch VFO/BFO
  ENCODER
  C
  A
  B
  SLC
  SDA
  Si5351A
  OLED
  VFO and BFO with Si5351 and Arduino
  By PU2CLR,
  March 26th, 2019

custom parts:
  Arduino Micro: Arduino Micro Microcontroller
  OLED Monochrome 128x64 0.96 inch: These displays are small, only about 1" diameter, but very readable due to the high contrast of an OLED display. This display is made of 128x64 individual white OLED pixels, each one is turned on or off by the controller chip. Because the display makes its own light, no backlight is required. This reduces the power required to run the OLED and is why the display has such high contrast; we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
  Adafruit Si5351A Clock Generator: Never hunt around for another crystal again, with the Si5351A clock generator breakout from Adafruit! This chip has a precision 25MHz crystal reference and internal PLL and dividers so it can generate just about any frequency, from <8KHz up to 150+ MHz. The Si5351A clock generator is an I2C controller clock generator. It uses the onboard precision clock to drive multiple PLL's and clock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
